# Fritzing sketch Lauflicht_Projekt (saved by Fritzing 0.9.3b)
circuit board: 8.46667cm x 5.64444cm
breadboards: 1

parts:
  LED1 = LED - 5mm [color="Red (633nm)" package="5 mm [THT]"]
  LED2 = LED - 5mm [color="Red (633nm)" package="5 mm [THT]"]
  LED3 = LED - 5mm [color="Red (633nm)" package="5 mm [THT]"]
  LED4 = LED - 5mm [color="Red (633nm)" package="5 mm [THT]"]
  LED5 = LED - 5mm [color="Red (633nm)" package="5 mm [THT]"]
  LED6 = LED - 5mm [color="Red (633nm)" package="5 mm [THT]"]
  R1 = Resistor [tolerance=±5% resistance=220 package=THT]
  R2 = Resistor [tolerance=±5% resistance=220 package=THT]
  R3 = Resistor [tolerance=±5% resistance=220 package=THT]
  R4 = Resistor [tolerance=±5% resistance=220 package=THT]
  R5 = Resistor [tolerance=±5% resistance=220 package=THT]
  R6 = Resistor [tolerance=±5% resistance=220 package=THT]
  RE1 = Rotary Encoder [package=THT]
  Part1 = Arduino Uno (Rev3)

nets:
  N1: LED1.cathode, LED2.cathode, LED3.cathode, LED4.cathode, LED5.cathode, LED6.cathode, RE1.EncoderPinB, Part1.GND
  N2: LED1.anode, R1.Pin_1
  N3: LED2.anode, R2.Pin_1
  N4: LED3.anode, R3.Pin_1
  N5: LED4.anode, R4.Pin_1
  N6: LED5.anode, R5.Pin_1
  N7: LED6.anode, R6.Pin_1
  N8: R1.Pin_0, Part1.D13/SCK
  N9: R2.Pin_0, Part1.D12/MISO
  N10: R3.Pin_0, Part1.D11_PWM/MOSI
  N11: R4.Pin_0, Part1.D10_PWM/SS
  N12: R5.Pin_0, Part1.D9_PWM
  N13: R6.Pin_0, Part1.D8
  N14: RE1.EncoderPinA, Part1.5V
  N15: RE1.EncoderPinC, Part1.A0

// code stored in the sketch: InsideCode.ino
int L1 = 13;
int L2 = 12;
int L3 = 11;
int L4 = 10;
int L5 = 9;
int L6 = 8;
int PAUSE = 200;
int const P1 = A0;
int potVal;
int zero = 50;


void setup() {
  // put your setup code here, to run once:
  pinMode(L1, OUTPUT);
  pinMode(L2, OUTPUT);
  pinMode(L3, OUTPUT);
  pinMode(L4, OUTPUT);
  pinMode(L5, OUTPUT);
  pinMode(L6, OUTPUT);
  Serial.begin(9600);
  
}

void loop() {
  // put your main code here, to run repeatedly:
  
  potVal = analogRead(P1);
  PAUSE = zero+potVal;
  Serial.print("potVal: ");
  Serial.print(PAUSE);
  
  digitalWrite(L1, HIGH);
  delay(PAUSE);
  digitalWrite(L1, LOW);

  potVal = analogRead(P1);
  PAUSE = zero+potVal;
  Serial.print("potVal: ");
  Serial.print(PAUSE);
  
  digitalWrite(L2, HIGH);
  delay(PAUSE);
  digitalWrite(L2, LOW);

  potVal = analogRead(P1);
  PAUSE = zero+potVal;
  Serial.print("potVal: ");
  Serial.print(PAUSE);

  digitalWrite(L3, HIGH);
  delay(PAUSE);
  digitalWrite(L3, LOW);

  potVal = analogRead(P1);
  PAUSE = zero+potVal;
  Serial.print("potVal: ");
  Serial.print(PAUSE);

  digitalWrite(L4, HIGH);
  delay(PAUSE);
  digitalWrite(L4, LOW);

  potVal = analogRead(P1);
  PAUSE = zero+potVal;
  Serial.print("potVal: ");
  Serial.print(PAUSE);

  digitalWrite(L5, HIGH);
  delay(PAUSE);
  digitalWrite(L5, LOW);

  potVal = analogRead(P1);
  PAUSE = zero+potVal;
  Serial.print("potVal: ");
  Serial.print(PAUSE);

  digitalWrite(L6, HIGH);
  delay(PAUSE);
  digitalWrite(L6, LOW);

  potVal = analogRead(P1);
  PAUSE = zero+potVal;
  Serial.print("potVal: ");
  Serial.print(PAUSE);
  
}
