# Fritzing sketch test (saved by Fritzing 0.9.3b)
breadboards: 1

parts:
  Bauteil2 = Arduino Uno (Rev3)
  R1 = Resistor [tolerance=±5% resistance=4.7k package=THT]
  R2 = Resistor [tolerance=±5% resistance=4.7k package=THT]
  Bauteil1 = Triple Axis Accelerometer Breakout - BMA280

nets:
  N1: Bauteil2.A4/SDA, R1.Pin_1, Bauteil1.SDA
  N2: Bauteil2.A5/SCL, R2.Pin_0, Bauteil1.SCX
  GND: Bauteil2.GND, Bauteil1.SDO, Bauteil1.GND_IO, Bauteil1.GND
  3V3: Bauteil2.3V3, R1.Pin_0, R2.Pin_1, Bauteil1.VDD_IO, Bauteil1.VDD

custom parts:
  Triple Axis Accelerometer Breakout - BMA280: Accelerometer for sensing three-dimensional orientation/acceleration on a breakout board.
